// Digital circuit vga.dig as structural Verilog
module vga (
  input  PCLK,
  input  nRD,
  input  nWR,
  input  nCS,
  input  [13:0] ADDR,
  input  [7:0] DATA,
  input  nIRQACK,
  input  [5:0] SCROLL,
  output [13:0] VADDR,
  output [7:0] VDATA
);

  wire _74157_1_p1, _74157_1_p13, _74157_1_p14, _74157_1_p15, _74377_2_p13, _74377_2_p14, _74377_2_p15,
       _74377_2_p16, _74377_2_p17, _74377_2_p18, _74377_2_p19, _74377_2_p20, BLANK, nCLOAD, nHSYNC, nPLOAD,
       nSHLOAD, nVSYNC, reset_1_out, u_vga_irq_n, u_vga_vwr_n;
  wire [7:0] CROM_d, VRAM_d;
  wire [10:0] u_vga_crow;

  vga #(.applicationType("IVERILOG")) u_vga (
    .pclk(PCLK), .rst_n(reset_1_out), .addr(ADDR), .data(DATA), .cs_n(nCS), .wr_n(nWR), .rd_n(nRD),
    .irqack_n(nIRQACK), .scroll(SCROLL), .irq_n(u_vga_irq_n), .vaddr(VADDR), .vdata(VDATA),
    .vwr_n(u_vga_vwr_n), .blank(BLANK), .hsync_n(nHSYNC), .vsync_n(nVSYNC), .shload_n(nSHLOAD),
    .pload_n(nPLOAD), .cload_n(nCLOAD), .crow(u_vga_crow[2:0]));  // open: vrd_n
  Reset reset_1 (.out(reset_1_out));
  LED led_1 (.in(u_vga_irq_n));
  LED led_2 (.in(u_vga_vwr_n));
  RAMAsync #(.AddrBits(14), .Bits(8)) ramasync_1 (.A({14{1'b0}}), .D({8{1'b0}}), .we(1'b0));  // open: Q
  ROM #(.AddrBits(14), .Bits(8)) VRAM (.A(VADDR), .sel(1'b1), .D(VRAM_d));
  // _74377 _74377_1: pin names not known; wires that end beside it: VRAM_d[0], 1'b1, 1'b0, VRAM_d[1], VRAM_d[2], VRAM_d[3], nPLOAD, VRAM_d[4], VRAM_d[5], VRAM_d[6], VRAM_d[7], PCLK, u_vga_crow[3], u_vga_crow[4], u_vga_crow[5], u_vga_crow[6], u_vga_crow[7], u_vga_crow[8], u_vga_crow[9], u_vga_crow[10]
  // _74377 _74377_2: pin names not known; wires that end beside it: VRAM_d[0], 1'b1, 1'b0, VRAM_d[1], VRAM_d[2], VRAM_d[3], nCLOAD, VRAM_d[4], VRAM_d[5], VRAM_d[6], VRAM_d[7], PCLK, _74377_2_p13, _74377_2_p14, _74377_2_p15, _74377_2_p16, _74377_2_p17, _74377_2_p18, _74377_2_p19, _74377_2_p20
  ROM #(.AddrBits(11), .Bits(8)) CROM (.A(u_vga_crow), .sel(1'b1), .D(CROM_d));
  // _74157 _74157_1: pin names not known; wires that end beside it: _74157_1_p1, _74377_2_p13, _74377_2_p14, _74377_2_p15, _74377_2_p16, _74377_2_p17, _74377_2_p18, _74377_2_p19, _74377_2_p20, BLANK, 1'b1, 1'b0, _74157_1_p13, _74157_1_p14, _74157_1_p15
  Break break_1 (.brk(PCLK));
  VGA vga_2 (.R(_74157_1_p13), .G(_74157_1_p14), .B(_74157_1_p15), .H(nHSYNC), .V(nVSYNC), .C(PCLK));
  // _74166 _74166_1: pin names not known; wires that end beside it: nSHLOAD, CROM_d[0], 1'b0, PCLK, 1'b1, CROM_d[1], CROM_d[2], CROM_d[3], CROM_d[4], CROM_d[5], CROM_d[6], CROM_d[7], 1'b1, 1'b0, 1'b1, _74157_1_p1

  // Notes on the sheet:
  //   PCLK: Hz: 25175000
  //   nRD: default 1
  //   nWR: default 1
  //   nCS: default 1
  //   nIRQACK: default 1
  //   contents of VRAM (hex, n*v repeats v):
  //   4d,6f,6a,20,73,74,61,72,79,20,74,6f,20,66,61,6e,61,74,79,6b,20
  //   ,77,65,64,6b,61,72,73,74,77,61,d,a,d,a,4d,6f,6a,20,73,74,61,72
  //   ,79,20,74,6f,20,66,61,6e,61,74,79,6b,20,77,65,64,6b,61,72,73,74
  //   ,77,61,2e,20,50,6f,6c,20,6d,69,65,73,7a,6b,61,6e,69,61,20,7a,61
  //   ,6a,65,62,61,6e,65,20,77,65,64,6b,61,6d,69,2c,20,6e,61,6a,67,6f
  //   ,72,7a,65,6a,2e,20,53,72,65,64,6e,69,6f,20,72,61,7a,20,77,20,6d
  //   ,69,65,73,69,61,63,75,20,6b,74,6f,73,20,77,64,65,70,6e,69,65,20
  //   ,77,20,6c,65,7a,61,63,79,20,6e,61,20,7a,69,65,6d,69,20,68,61,63
  //   ,7a,79,6b,20,63,7a,79,20,6b,6f,74,77,69,63,65,20,69,20,74,72,7a
  //   ,65,62,61,20,77,79,63,69,61,67,61,63,20,77,20,73,7a,70,69,74,61
  //   ,6c,75,2c,20,62,6f,20,6d,61,6a,61,20,7a,61,64,7a,69,6f,72,79,20
  //   ,6e,61,20,6b,6f,6e,63,75,2e,20,57,20,73,77,6f,69,6d,20,64,77,75
  //   ,64,7a,69,65,73,74,6f,64,77,75,6c,65,74,6e,69,6d,20,7a,79,63,69
  //   ,75,20,6a,75,7a,20,7a,20,31,30,20,72,61,7a,79,20,62,79,6c,65,6d
  //   ,20,6e,61,20,74,61,6b,69,6d,20,7a,61,62,69,65,67,75,2e,20,54,79
  //   ,64,7a,69,65,6e,20,74,65,6d,75,20,70,6f,73,7a,65,64,6c,65,6d,20
  //   ,6e,61,20,6a,61,6b,69,65,73,20,6c,6f,73,6f,77,65,20,62,61,64,61
  //   ,6e,69,61,2c,20,74,6f,20,62,61,62,61,20,7a,20,72,65,63,65,70,63
  //   ,6a,69,20,6a,61,6b,20,6d,6e,69,65,20,74,79,6c,6b,6f,20,7a,6f,62
  //   ,61,63,7a,79,6c,61,2c,20,74,6f,20,6b,61,7a,61,6c,61,20,62,75,74
  //   ,61,20,73,63,69,61,67,61,63,20,78,44,2c,20,62,6f,20,6d,79,73,6c
  //   ,61,6c,61,2c,20,7a,65,20,7a,6e,6f,77,75,20,68,61,6b,20,77,20,6e
  //   ,6f,64,7a,65,2e,d,a,d,a,44,72,75,67,61,20,70,6f,6c,6f,77,61,20
  //   ,6d,69,65,73,7a,6b,61,6e,69,61,20,7a,61,6a,65,62,61,6e,61,20,2c,2c
  //   ,57,65,64,6b,61,72,7a,65,6d,20,50,6f,6c,73,6b,69,6d,22,2c,20,2c,2c
  //   ,53,77,69,61,74,65,6d,20,57,65,64,6b,61,72,7a,61,22,2c,20,2c,2c
  //   ,53,75,70,65,72,20,4b,61,72,70,69,65,6d,22,20,78,44,20,69,74,70
  //   ,2e,20,43,6f,20,74,79,64,7a,69,65,6e,20,6f,6a,63,69,65,63,20,72
  //   ,6f,62,69,20,6f,62,6a,61,7a,64,20,70,6f,20,77,73,7a,79,73,74,6b
  //   ,69,63,68,20,6b,69,6f,73,6b,61,63,68,20,77,20,6d,69,65,73,63,69
  //   ,65,2c,20,7a,65,62,79,20,73,6b,6f,6d,70,6c,65,74,6f,77,61,63,20
  //   ,77,73,7a,79,73,74,6b,69,65,20,77,65,64,6b,61,72,73,6b,69,65,20
  //   ,74,79,67,6f,64,6e,69,6b,69,2e,20,42,79,6c,65,6d,20,6e,61,20,74
  //   ,79,6c,65,20,67,6c,75,70,69,2c,20,7a,65,20,6e,61,75,63,7a,79,6c
  //   ,65,6d,20,67,6f,20,69,6e,74,6f,20,69,6e,74,65,72,6e,65,74,79,2c
  //   ,20,62,6f,20,6d,79,73,6c,61,6c,65,6d,2c,20,7a,65,20,74,72,6f,63
  //   ,68,65,20,70,69,65,6e,69,65,64,7a,79,20,7a,61,6f,73,7a,63,7a,65
  //   ,64,7a,69,6d,79,20,6e,61,20,74,79,63,68,20,67,61,7a,65,74,6b,61
  //   ,63,68,2c,20,61,6c,65,20,74,65,72,61,7a,20,6e,69,65,20,64,6f,73
  //   ,79,63,2c,20,7a,65,20,6a,65,20,6b,75,70,75,6a,65,2c,20,74,6f,20
  //   ,6a,65,73,7a,63,7a,65,20,73,69,65,64,7a,69,20,6e,61,20,6a,61,6b
  //   ,69,63,68,73,20,66,6f,72,61,63,68,20,64,6c,61,20,77,65,64,6b,61
  //   ,72,7a,79,20,69,20,6b,72,65,63,69,20,67,6f,77,6e,6f,62,75,72,7a
  //   ,65,20,7a,20,69,6e,6e,79,6d,69,20,77,65,64,6b,61,72,7a,61,6d,69
  //   ,20,6f,20,6e,61,6a,6c,65,70,73,7a,65,20,7a,61,6e,65,74,79,20,69
  //   ,74,70,2e,20,50,6f,74,72,61,66,69,20,64,72,7a,65,63,20,6d,6f,72
  //   ,64,65,20,64,6f,20,6d,6f,6e,69,74,6f,72,61,20,61,6c,62,6f,20,77
  //   ,79,70,69,65,72,64,6f,6c,69,63,20,6b,6c,61,77,69,61,74,75,72,65
  //   ,20,7a,61,20,6f,6b,6e,6f,2e,20,4b,69,65,64,79,73,20,6f,6a,63,69
  //   ,65,63,20,6d,6e,69,65,20,77,6b,75,72,77,69,6c,2c,20,74,6f,20,7a
  //   ,61,6c,6f,7a,79,6c,65,6d,20,74,61,6d,20,6b,6f,6e,74,6f,20,69,20
  //   ,67,6f,20,74,72,6f,6c,6c,6f,77,61,6c,65,6d,2c,20,70,69,73,7a,61
  //   ,63,20,77,20,6a,65,67,6f,20,74,65,6d,61,74,61,63,68,20,6a,61,6b
  //   ,69,65,73,20,6c,6f,73,6f,77,65,20,67,6c,75,70,6f,74,79,2c,20,74
  //   ,79,70,75,20,2c,2c,6b,61,72,61,73,69,65,20,6a,65,64,7a,6f,20,67
  //   ,75,77,6e,6f,22,2e,20,4d,61,74,6b,61,20,6e,69,65,20,6e,61,64,61
  //   ,7a,61,6c,61,20,7a,20,67,6f,74,6f,77,61,6e,69,65,6d,20,62,69,67
  //   ,6f,73,75,20,6e,61,20,75,73,70,6f,6b,6f,6a,65,6e,69,65,2e,20,41
  //   ,68,61,2c,20,6d,61,20,6a,75,7a,20,6e,61,20,66,6f,72,75,6d,20,72
  //   ,61,6e,67,65,20,53,55,4d,2c,20,7a,61,20,6e,61,6a,65,62,61,6e,69
  //   ,65,20,31,30,20,74,79,73,69,65,63,79,20,70,6f,73,74,6f,77,2e,d
  //   ,a,d,a,4a,61,6b,20,6a,65,73,74,20,63,69,65,70,6c,6f,2c,20,74,6f
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  //   contents of CROM (hex, n*v repeats v):
  //   8*ff,81,7e,5a,7e,62,46,7e,81,81,0,24,0,1c,38,0,81,93,1,1,1,83
  //   ,c7,ef,ff,ef,c7,83,1,83,c7,ef,ff,c7,83,c7,1,1,ef,ef,83,ff,e7,c3
  //   ,81,0,81,e7,81,ff,ff,e7,c3,c3,e7,ff,ff,0,0,18,3c,3c,18,0,0,ff
  //   ,c3,99,bd,bd,99,c3,ff,0,3c,66,42,42,66,3c,0,f0,f8,f0,82,33,33,33
  //   ,87,c3,99,99,99,c3,e7,81,e7,c0,cc,c0,cf,cf,8f,f,1f,80,9c,80,9c,9c
  //   ,98,19,3f,66,a5,c3,18,18,c3,a5,66,7f,1f,7,1,7,1f,7f,ff,fd,f1,c1
  //   ,1,c1,f1,fd,ff,e7,c3,81,e7,e7,81,c3,e7,5*99,ff,99,ff,80,24,24
  //   ,84,e4,e4,e4,ff,c0,9f,83,99,99,c1,f9,3,4*ff,81,81,81,ff,e7,c3
  //   ,81,e7,81,c3,e7,0,e7,c3,81,4*e7,ff,4*e7,81,c3,e7,ff,ff,e7,f3,1
  //   ,f3,e7,ff,ff,ff,cf,9f,1,9f,cf,4*ff,3f,3f,3f,1,ff,ff,ff,db,99,0
  //   ,99,db,ff,ff,ff,e7,c3,81,0,0,ff,ff,ff,0,0,81,c3,e7,10*ff,5*e7
  //   ,ff,e7,ff,93,93,93,5*ff,93,93,1,93,1,93,93,ff,e7,81,3f,83,f9,3
  //   ,e7,ff,ff,39,33,e7,cf,99,39,ff,c7,93,c7,89,23,33,89,ff,cf,cf,9f
  //   ,5*ff,f3,e7,cf,cf,cf,e7,f3,ff,cf,e7,f3,f3,f3,e7,cf,ff,ff,99,c3
  //   ,0,c3,99,ff,ff,ff,e7,e7,81,e7,e7,7*ff,e7,e7,cf,ff,ff,ff,81,9*ff
  //   ,e7,e7,ff,f9,f3,e7,cf,9f,3f,7f,ff,83,31,21,9,19,39,83,ff,e7,c7
  //   ,4*e7,81,ff,83,39,f9,83,3f,3f,1,ff,3,f9,f9,c3,f9,f9,3,ff,f3,33,33,33
  //   ,1,f3,f3,ff,1,3f,3,f9,f9,39,83,ff,83,3f,3f,3,39,39,83,ff,1,f9,f9
  //   ,f3,e7,cf,cf,ff,83,39,39,83,39,39,83,ff,83,39,39,81,f9,f9,83,ff,ff
  //   ,e7,e7,ff,ff,e7,e7,ff,ff,e7,e7,ff,ff,e7,e7,cf,f3,e7,cf,9f,cf,e7
  //   ,f3,ff,ff,ff,81,ff,81,ff,ff,ff,cf,e7,f3,f9,f3,e7,cf,ff,c3,99,f3
  //   ,e7,e7,ff,e7,ff,83,39,21,21,21,3f,81,ff,c7,93,39,39,1,39,39,ff
  //   ,3,39,39,3,39,39,3,ff,83,39,3f,3f,3f,39,83,ff,7,33,39,39,39,33
  //   ,7,ff,1,3f,3f,7,3f,3f,1,ff,1,3f,3f,7,3f,3f,3f,ff,83,39,3f,3f,31
  //   ,39,83,ff,39,39,39,1,39,39,39,ff,81,5*e7,81,ff,5*f9,39,83,ff,39
  //   ,33,27,f,27,33,39,ff,6*3f,1,ff,39,11,1,1,29,39,39,ff,39,19,9,21
  //   ,31,39,39,ff,83,5*39,83,ff,3,39,39,3,3f,3f,3f,ff,83,39,39,39,29
  //   ,21,83,f9,3,39,39,3,27,33,39,ff,83,39,3f,83,f9,39,83,ff,0,6*e7
  //   ,ff,6*39,1,ff,5*39,83,c7,ff,4*39,29,1,93,ff,39,39,93,c7,93,39,39
  //   ,ff,39,39,39,83,e7,cf,1f,ff,1,f9,f3,e7,cf,9f,1,ff,c3,5*cf,c3,ff
  //   ,3f,9f,cf,e7,f3,f9,fd,ff,c3,5*f3,c3,ff,ef,c7,93,39,11*ff,0,e7,e7
  //   ,f3,7*ff,83,f9,81,39,81,ff,3f,3f,3f,3,39,39,3,ff,ff,ff,83,39,3f
  //   ,39,83,ff,f9,f9,f9,81,39,39,81,ff,ff,ff,83,39,1,3f,83,ff,e3,c9
  //   ,cf,87,cf,cf,87,ff,ff,ff,81,39,39,81,f9,3,3f,3f,3,4*39,ff,e7,ff
  //   ,c7,e7,e7,e7,c3,ff,f9,ff,4*f9,39,83,3f,3f,33,27,7,33,39,ff,c7
  //   ,5*e7,c3,ff,ff,ff,33,1,1,29,29,ff,ff,ff,3,4*39,ff,ff,ff,83,39,39,39
  //   ,83,ff,ff,ff,3,39,39,3,3f,3f,ff,ff,81,39,39,81,f9,f9,ff,ff,3,39
  //   ,3f,3f,3f,ff,ff,ff,81,3f,83,f9,3,ff,e7,e7,81,e7,e7,e7,f1,ff,ff,ff
  //   ,4*39,81,ff,ff,ff,39,39,39,83,c7,ff,ff,ff,39,39,29,1,93,ff,ff,ff
  //   ,39,93,c7,93,39,ff,ff,ff,39,39,39,81,f9,3,ff,ff,1,f3,c7,9f,1,ff
  //   ,f1,e7,e7,8f,e7,e7,f1,ff,e7,e7,e7,ff,e7,e7,e7,ff,8f,e7,e7,f1,e7,e7
  //   ,8f,ff,89,23,7*ff,ef,c7,93,39,39,1,ff,83,39,3f,3f,3f,29,83,cf
  //   ,39,ff,4*39,81,ff,f1,ff,83,39,1,3f,83,ff,81,7e,c3,f9,81,39,81
  //   ,ff,99,ff,83,f9,81,39,81,ff,1f,ff,83,f9,81,39,81,ff,e7,e7,83,f9
  //   ,81,39,81,ff,ff,ff,83,39,3f,29,83,cf,81,7e,83,39,1,3f,83,ff,99
  //   ,ff,83,39,1,3f,83,ff,1f,ff,83,39,1,3f,83,ff,99,ff,c7,e7,e7,e7
  //   ,c3,ff,83,7d,c7,e7,e7,e7,c3,ff,8f,ff,c7,e7,e7,e7,c3,ff,39,ef,83
  //   ,39,1,39,39,ff,c7,c7,ff,83,39,1,39,ff,f1,ff,1,3f,7,3f,1,ff,ff,ff
  //   ,80,f3,80,33,80,ff,c0,93,33,0,33,33,30,ff,83,7d,83,39,39,39,83
  //   ,ff,99,ff,83,39,39,39,83,ff,1f,ff,83,39,39,39,83,ff,83,7d,ff,39,39,39
  //   ,81,ff,1f,ff,4*39,81,ff,99,ff,99,99,99,c1,f9,83,39,83,4*39,83
  //   ,ff,39,ff,4*39,1,ff,e7,e7,81,27,27,27,81,e7,c7,93,9f,f,9f,99,3
  //   ,ff,99,99,c3,e7,81,e7,81,e7,7,33,33,5,39,30,39,3c,f1,e4,e7,c3
  //   ,e7,e7,27,8f,f1,ff,83,f9,81,39,81,ff,e3,ff,c7,e7,e7,e7,c3,ff,f1
  //   ,ff,83,39,39,39,83,ff,f1,ff,4*39,81,ff,ff,1,ff,3,39,39,39,ff,1
  //   ,ff,39,19,9,21,31,ff,c3,93,93,c1,ff,81,ff,ff,c3,99,99,c3,ff,81
  //   ,ff,ff,e7,ff,e7,e7,cf,99,c3,4*ff,3,3f,3f,5*ff,3,f3,f3,ff,ff,39
  //   ,33,27,c0,9c,30,73,f0,3c,39,33,24,c8,92,30,fc,e7,ff,5*e7,ff,ff
  //   ,cc,99,33,99,cc,ff,ff,ff,33,99,cc,99,33,ff,ff,dd,77,dd,77,dd,77
  //   ,dd,77,aa,55,aa,55,aa,55,aa,55,22,88,22,88,22,88,22,88,12*e7,7
  //   ,5*e7,7,e7,7,e7,e7,e7,4*c9,9,c9,c9,c9,4*ff,1,c9,c9,c9,ff,ff,7
  //   ,e7,7,e7,e7,e7,c9,c9,9,f9,9,11*c9,ff,ff,1,f9,9,5*c9,9,f9,1,ff,ff,ff
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endmodule

/* Code of vga:
module vga (
	input pclk,
	input rst_n,

	// MCU interface
	input [13:0] addr,
	input [7:0] data, // should be inout!
	input cs_n,
	input wr_n,
	input rd_n,
	output reg irq_n,
	input irqack_n,
	input [5:0] scroll,

	// VRAM
	output [13:0] vaddr,
	output [7:0] vdata, // should be inout!
	output vrd_n,
	output vwr_n,

	// VGA control
	output reg blank,
	output reg hsync_n,
	output reg vsync_n,
	output reg shload_n,
	output pload_n,
	output cload_n,
	output [2:0] crow
);

reg [9:0] col_i;
reg [9:0] row_i;

// counters
always @(posedge pclk, negedge rst_n) begin
	if (~rst_n) begin
		col_i <= 0;
		row_i <= 0;
	end else begin
		col_i <= col_i + 1;
		if (col_i == 799) begin
			col_i <= 0;
			row_i <= row_i + 1;
			if (row_i == 524)
				row_i <= 0;
		end
	end
end

// column counter delay
reg [9:2] col_b;

always @(posedge pclk, negedge rst_n) begin
	if (~rst_n)
		col_b[9:2] <= 8'b0;
	else
		col_b[9:2] <= col_i[9:2];
end

// blanking
reg hblank;
reg vblank;

always @(posedge pclk, negedge rst_n) begin
	if (~rst_n)
		vblank <= 1;
	else begin
		if (row_i >= 480)
			vblank <= 1;
		else
			vblank <= 0;
	end
end

always @(posedge pclk, negedge rst_n) begin
	if (~rst_n)
		hblank <= 1;
	else begin
		if (col_i < (8 - 2) || col_i >= (640 - 2 + 8))
			hblank <= 1;
		else
			hblank <= 0;
	end
end

always @(posedge pclk, negedge rst_n) begin
	if (~rst_n) begin
		blank <= 1;
	end else begin
		blank <= hblank || vblank;
	end
end

// interrupt
wire irq_reset;

assign irq_reset = ~rst_n || ~irqack_n;
always @(posedge vblank, posedge irq_reset) begin
	if (irq_reset)
		irq_n <= 1;
	else
		irq_n <= 0;
end

// hsync
reg hsync_i;

always @(posedge pclk, negedge rst_n) begin
	if (~rst_n) begin
		hsync_i <= 0;
		hsync_n <= 0;
	end else begin
		if (col_i >= (640 + 16 + 8 - 1) && col_i < (640 + 16 + 8 + 96 - 1))
			hsync_i <= 1;
		else
			hsync_i <= 0;

		hsync_n <= ~hsync_i;
	end
end

// vsync
reg vsync_i;

always @(posedge pclk, negedge rst_n) begin
	if (~rst_n) begin
		vsync_i <= 0;
		vsync_n <= 0;
	end else begin
		if (row_i >= (480 + 10) && row_i < (480 + 10 + 2))
			vsync_i <= 1;
		else
			vsync_i <= 0;

		vsync_n <= ~vsync_i;
	end
end

// registers load
wire color;

always @(posedge pclk, negedge rst_n) begin
	if (~rst_n)
		shload_n <= 1;
	else begin
		if (col_i[2:0] == 3'b111)
			shload_n <= 0;
		else
			shload_n <= 1;
	end
end

assign color = col_b[2];
assign pload_n = color;
assign cload_n = shload_n;

// character generator
assign crow = row_i[2:0];

// VRAM and MCU interface
assign vwr_n = (~cs_n && ~wr_n) ? 1'b0 : 1'b1;
assign vrd_n = ~vwr_n;
assign vdata = (~cs_n && ~wr_n) ? data : 8'bz;
//assign data = (~cs_n && ~rd_n) ? vdata : 8'bz;

wire [5:0] row_added;

assign row_added = row_i[8:3] + scroll;
assign vaddr = ~cs_n ? addr : { color, row_added, col_b[9:3] };

endmodule
*/
